# Fritzing sketch Version1_onlyMotor (saved by Fritzing 0.9.2b)
circuit board: 2.68871cm x 4.04518cm
breadboards: 1

parts:
  Q1 = Basic FET P-Channel [part_number="IRF 4905" package="TO220 [THT]"]
  M1 = DC Motor
  Teensy_3_1 = Teensy 3.1

nets (from the breadboard view):
  N1: Q1.gate, Teensy_3_1.D12
  N2: Q1.drain, M1.pin_1
  N3: Q1.source, Teensy_3_1.Vin
  N4: M1.pin_2, Teensy_3_1.GND
