# Fritzing sketch Version2_WithButton (saved by Fritzing 0.9.2b)
breadboards: 1

parts:
  Teensy_3_1 = Teensy 3.1
  Q1 = Basic FET P-Channel [package="TO220 [THT]"]
  M1 = DC Motor
  S1 = Pushbutton [package="[THT]"]

nets:
  N1: Teensy_3_1.GND, M1.pin_2, S1.Pin_3, S1.Pin_4
  N2: Teensy_3_1.D8, S1.Pin_1, S1.Pin_2
  N3: Teensy_3_1.D12, Q1.gate
  N4: Teensy_3_1.Vin, Q1.source
  N5: Q1.drain, M1.pin_1
